# Fritzing sketch raspberry-sensors (saved by Fritzing 0.9.3b)

parts:
  Raspberry_Pi_1 = Raspberry Pi 3 [part_number=RPI-3-V1.2]
  Part2 = BME280 Breakout

nets:
  3V3: Raspberry_Pi_1.3v3, Raspberry_Pi_1.3V3, Part2.3.3V
  N1: Raspberry_Pi_1.GPIO2, Part2.SDI/SDA
  N2: Raspberry_Pi_1.GPIO3, Part2.SCK/SCL
  GND: Raspberry_Pi_1.GND, Part2.GND

notes:
  5V DC via Instruments circuit
  USB GPS dongle
  Connected to WiFi AP
  Barometer, humidity, temperature
